// Logisim project Circuit.circ as structural Verilog: 3 circuits, main circuit main
module main (
  input  Cin,
  input  A,
  input  B,
  input  Less,
  input  [1:0] Operation,
  input  Ainvert,
  input  Binvert,
  output Result,
  output Cout,
  output Set
);

  wire and_1_out, multiplexer_1_out, multiplexer_2_out, not_1_out, not_2_out, or_1_out;

  not not_1 (not_1_out, A);
  not not_2 (not_2_out, B);
  Multiplexer #(.enable("false")) multiplexer_1 (.in0(A), .in1(not_1_out), .out(multiplexer_1_out), .sel(Ainvert));
  Multiplexer #(.enable("false")) multiplexer_2 (.in0(B), .in1(not_2_out), .out(multiplexer_2_out), .sel(Binvert));
  and and_1 (and_1_out, multiplexer_1_out, multiplexer_2_out);
  or or_1 (or_1_out, multiplexer_1_out, multiplexer_2_out);
  Adder #(.width(1)) adder_1 (.a(multiplexer_1_out), .b(multiplexer_2_out), .out(Set), .cin(Cin), .cout(Cout));
  Multiplexer #(.enable("false"), .select(2)) multiplexer_3 (
    .in0(and_1_out), .in1(or_1_out), .in2(Set), .in3(Less), .out(Result), .sel(Operation));
endmodule

module ALU16bit (
  input  [15:0] A,
  input  in_2,
  input  in_3,
  input  [1:0] in_4,
  input  [15:0] B,
  output [15:0] Result,
  output Zero
);

  wire main_1_cout, main_2_cout, main_3_cout, main_4_cout, main_5_cout, main_6_cout, main_7_cout,
       main_8_cout, main_9_cout, main_10_cout, main_11_cout, main_12_cout, main_13_cout, main_14_cout,
       main_15_cout, main_16_set;

  main main_1 (
    .Cout(main_1_cout), .Result(Result[0]), .A(A[0]), .B(B[0]), .Less(main_16_set), .Ainvert(in_2),
    .Binvert(in_3), .Operation(in_4), .Cin(in_3));  // open: Set
  main main_2 (
    .Cout(main_2_cout), .Result(Result[1]), .A(A[1]), .B(B[1]), .Less(1'b0), .Ainvert(in_2), .Binvert(in_3),
    .Operation(in_4), .Cin(main_1_cout));  // open: Set
  main main_3 (
    .Cout(main_3_cout), .Result(Result[2]), .A(A[2]), .B(B[2]), .Less(1'b0), .Ainvert(in_2), .Binvert(in_3),
    .Operation(in_4), .Cin(main_2_cout));  // open: Set
  main main_4 (
    .Cout(main_4_cout), .Result(Result[3]), .A(A[3]), .B(B[3]), .Less(1'b0), .Ainvert(in_2), .Binvert(in_3),
    .Operation(in_4), .Cin(main_3_cout));  // open: Set
  main main_5 (
    .Cout(main_5_cout), .Result(Result[4]), .A(A[4]), .B(B[4]), .Less(1'b0), .Ainvert(in_2), .Binvert(in_3),
    .Operation(in_4), .Cin(main_4_cout));  // open: Set
  main main_6 (
    .Cout(main_6_cout), .Result(Result[5]), .A(A[5]), .B(B[5]), .Less(1'b0), .Ainvert(in_2), .Binvert(in_3),
    .Operation(in_4), .Cin(main_5_cout));  // open: Set
  main main_7 (
    .Cout(main_7_cout), .Result(Result[6]), .A(A[6]), .B(B[6]), .Less(1'b0), .Ainvert(in_2), .Binvert(in_3),
    .Operation(in_4), .Cin(main_6_cout));  // open: Set
  main main_8 (
    .Cout(main_8_cout), .Result(Result[7]), .A(A[7]), .B(B[7]), .Less(1'b0), .Ainvert(in_2), .Binvert(in_3),
    .Operation(in_4), .Cin(main_7_cout));  // open: Set
  main main_9 (
    .Cout(main_9_cout), .Result(Result[8]), .A(A[8]), .B(B[8]), .Less(1'b0), .Ainvert(in_2), .Binvert(in_3),
    .Operation(in_4), .Cin(main_8_cout));  // open: Set
  main main_10 (
    .Cout(main_10_cout), .Result(Result[9]), .A(A[9]), .B(B[9]), .Less(1'b0), .Ainvert(in_2), .Binvert(in_3),
    .Operation(in_4), .Cin(main_9_cout));  // open: Set
  main main_11 (
    .Cout(main_11_cout), .Result(Result[10]), .A(A[10]), .B(B[10]), .Less(1'b0), .Ainvert(in_2),
    .Binvert(in_3), .Operation(in_4), .Cin(main_10_cout));  // open: Set
  main main_12 (
    .Cout(main_12_cout), .Result(Result[11]), .A(A[11]), .B(B[11]), .Less(1'b0), .Ainvert(in_2),
    .Binvert(in_3), .Operation(in_4), .Cin(main_11_cout));  // open: Set
  main main_13 (
    .Cout(main_13_cout), .Result(Result[12]), .A(A[12]), .B(B[12]), .Less(1'b0), .Ainvert(in_2),
    .Binvert(in_3), .Operation(in_4), .Cin(main_12_cout));  // open: Set
  main main_14 (
    .Cout(main_14_cout), .Result(Result[13]), .A(A[13]), .B(B[13]), .Less(1'b0), .Ainvert(in_2),
    .Binvert(in_3), .Operation(in_4), .Cin(main_13_cout));  // open: Set
  main main_15 (
    .Cout(main_15_cout), .Result(Result[14]), .A(A[14]), .B(B[14]), .Less(1'b0), .Ainvert(in_2),
    .Binvert(in_3), .Operation(in_4), .Cin(main_14_cout));  // open: Set
  main main_16 (
    .Set(main_16_set), .Result(Result[15]), .A(A[15]), .B(B[15]), .Less(1'b0), .Ainvert(in_2),
    .Binvert(in_3), .Operation(in_4), .Cin(main_15_cout));  // open: Cout
  nor nor_1 (Zero, Result[0], Result[1], Result[2], Result[3], Result[4], Result[5], Result[6], Result[7], Result[8], Result[9], Result[10], Result[11], Result[12], Result[13], Result[14], Result[15]);
endmodule

module ControlUnit (
  input  Op5,
  input  Op4,
  input  Op3,
  input  Op2,
  input  Op1,
  input  Op0,
  output RegDst,
  output ALUSrc,
  output MemtoReg,
  output RegWrite,
  output MemRead,
  output Memwrite,
  output Branch,
  output ALUOp1,
  output ALUOp0
);

  wire and_5_out;

  and and_1 (ALUOp1, ~Op5, ~Op4, ~Op3, ~Op2, ~Op1, ~Op0);  // AND_Gate
  and and_2 (MemRead, Op5, ~Op4, ~Op3, ~Op2, Op1, Op0);  // AND_Gate
  and and_3 (Memwrite, Op5, ~Op4, Op3, ~Op2, Op1, Op0);  // AND_Gate
  and and_4 (ALUOp0, ~Op5, ~Op4, ~Op3, Op2, ~Op1, ~Op0);  // AND_Gate
  and and_5 (and_5_out, ~Op5, ~Op4, Op3, ~Op2, ~Op1, ~Op0);  // AND_Gate
  or or_1 (ALUSrc, MemRead, and_5_out, Memwrite);
  or or_2 (RegWrite, ALUOp1, and_5_out, MemRead);

  assign Branch = ALUOp0;
  assign MemtoReg = MemRead;
  assign RegDst = ALUOp1;

  // Notes on the sheet:
  //   Rformat
  //   lw
  //   sw
  //   beq
  //   addi
endmodule
